# Fritzing sketch crankcrankgif (saved by Fritzing 0.8.3b)
breadboards: 1

parts:
  Raspberry_Pi_rev1 = Raspberry Pi rev2
  LED1 = RGB LED - (4 legs) [package="5 mm [THT]"]
  RE1 = Rotary Encoder [package=THT]
  R1 = Resistor [tolerance=±5% resistance=1k package=THT]
  R2 = Resistor [tolerance=±5% resistance=1k package=THT]
  R3 = Resistor [tolerance=±5% resistance=1k package=THT]

nets:
  N1: Raspberry_Pi_rev1.GIPO_3, RE1.EncoderPinA
  N2: Raspberry_Pi_rev1.GND, LED1.common_anode, RE1.EncoderPinC
  N3: Raspberry_Pi_rev1.GPIO_23, RE1.EncoderPinB
  N4: Raspberry_Pi_rev1.GPIO4, R1.Pin_0
  N5: Raspberry_Pi_rev1.GPIO_24, R2.Pin_0
  N6: Raspberry_Pi_rev1.GPIO_25, R3.Pin_0
  N7: LED1.red_cathode, R3.Pin_1
  N8: LED1.green_cathode, R2.Pin_1
  N9: LED1.blue_cathode, R1.Pin_1
